// Digital circuit RAM+ALU.dig as structural Verilog
module RAM_ALU (
  input  write_into_register_A,
  input  write_into_register_B,
  input  in_3,
  input  in_4,
  input  in_5,
  input  in_6,
  input  Add_Subtract,
  input  write_into_RAM,
  input  RAM_address_selector_bit_0,
  input  RAM_address_selector_bit_1,
  output out_7,
  output out_8,
  output out_9,
  output out_10
);

  wire add_2_c_o, add_3_c_o, add_4_c_o, and_1_out, and_2_out, and_3_out, and_4_out, and_5_out, and_6_out,
       and_7_out, and_8_out, and_9_out, and_10_out, and_11_out, and_12_out, and_13_out, and_14_out,
       and_15_out, and_16_out, and_17_out, and_18_out, and_19_out, and_20_out, and_21_out, and_22_out,
       and_23_out, and_24_out, d_ff_1_q, d_ff_2_q, d_ff_3_q, d_ff_4_q, d_ff_5_q, d_ff_6_q, d_ff_7_q,
       d_ff_8_q, d_ff_9_q, d_ff_10_q, d_ff_11_q, d_ff_12_q, d_ff_13_q, d_ff_14_q, d_ff_15_q, d_ff_16_q,
       d_ff_17_q, d_ff_18_q, d_ff_19_q, d_ff_20_q, d_ff_21_q, d_ff_22_q, d_ff_23_q, d_ff_24_q, not_1_out,
       not_2_out, not_3_out, not_4_out, or_1_out, or_2_out, or_3_out, or_4_out, or_5_out, or_6_out, or_7_out,
       or_8_out, or_9_out, or_10_out, or_11_out, or_12_out, switch_9_a, switch_10_a, switch_11_a,
       switch_12_a, xor_1_out, xor_2_out, xor_3_out, xor_4_out;

  not not_1 (not_1_out, RAM_address_selector_bit_0);
  not not_2 (not_2_out, RAM_address_selector_bit_1);
  not not_3 (not_3_out, RAM_address_selector_bit_1);
  not not_4 (not_4_out, RAM_address_selector_bit_0);
  and and_1 (and_1_out, write_into_RAM, and_2_out);
  and and_2 (and_2_out, not_1_out, not_2_out);
  and and_3 (and_3_out, write_into_RAM, and_4_out);
  and and_4 (and_4_out, RAM_address_selector_bit_0, not_3_out);
  and and_5 (and_5_out, write_into_RAM, and_6_out);
  and and_6 (and_6_out, not_4_out, RAM_address_selector_bit_1);
  and and_7 (and_7_out, write_into_RAM, and_8_out);
  and and_8 (and_8_out, RAM_address_selector_bit_0, RAM_address_selector_bit_1);
  D_FF d_ff_1 (.D(out_8), .C(and_1_out), .Q(d_ff_1_q));  // open: nQ
  D_FF d_ff_2 (.D(out_7), .C(and_1_out), .Q(d_ff_2_q));  // open: nQ
  D_FF d_ff_3 (.D(out_8), .C(and_3_out), .Q(d_ff_3_q));  // open: nQ
  D_FF d_ff_4 (.D(out_7), .C(and_3_out), .Q(d_ff_4_q));  // open: nQ
  D_FF d_ff_5 (.D(out_8), .C(and_5_out), .Q(d_ff_5_q));  // open: nQ
  D_FF d_ff_6 (.D(out_7), .C(and_5_out), .Q(d_ff_6_q));  // open: nQ
  D_FF d_ff_7 (.D(out_8), .C(and_7_out), .Q(d_ff_7_q));  // open: nQ
  D_FF d_ff_8 (.D(out_7), .C(and_7_out), .Q(d_ff_8_q));  // open: nQ
  D_FF d_ff_9 (.D(out_10), .C(and_1_out), .Q(d_ff_9_q));  // open: nQ
  D_FF d_ff_10 (.D(out_9), .C(and_1_out), .Q(d_ff_10_q));  // open: nQ
  D_FF d_ff_11 (.D(out_10), .C(and_3_out), .Q(d_ff_11_q));  // open: nQ
  D_FF d_ff_12 (.D(out_9), .C(and_3_out), .Q(d_ff_12_q));  // open: nQ
  D_FF d_ff_13 (.D(out_10), .C(and_5_out), .Q(d_ff_13_q));  // open: nQ
  D_FF d_ff_14 (.D(out_9), .C(and_5_out), .Q(d_ff_14_q));  // open: nQ
  D_FF d_ff_15 (.D(out_10), .C(and_7_out), .Q(d_ff_15_q));  // open: nQ
  D_FF d_ff_16 (.D(out_9), .C(and_7_out), .Q(d_ff_16_q));  // open: nQ
  and and_9 (and_9_out, d_ff_9_q, and_2_out);
  and and_10 (and_10_out, d_ff_10_q, and_2_out);
  and and_11 (and_11_out, d_ff_1_q, and_2_out);
  and and_12 (and_12_out, d_ff_2_q, and_2_out);
  and and_13 (and_13_out, d_ff_11_q, and_4_out);
  and and_14 (and_14_out, d_ff_12_q, and_4_out);
  and and_15 (and_15_out, d_ff_3_q, and_4_out);
  and and_16 (and_16_out, d_ff_4_q, and_4_out);
  and and_17 (and_17_out, d_ff_13_q, and_6_out);
  and and_18 (and_18_out, d_ff_14_q, and_6_out);
  and and_19 (and_19_out, d_ff_5_q, and_6_out);
  and and_20 (and_20_out, d_ff_6_q, and_6_out);
  and and_21 (and_21_out, d_ff_15_q, and_8_out);
  and and_22 (and_22_out, d_ff_16_q, and_8_out);
  and and_23 (and_23_out, d_ff_7_q, and_8_out);
  and and_24 (and_24_out, d_ff_8_q, and_8_out);
  or or_1 (or_1_out, and_9_out, and_13_out);
  or or_2 (or_2_out, and_17_out, and_21_out);
  or or_3 (or_3_out, and_10_out, and_14_out);
  or or_4 (or_4_out, and_18_out, and_22_out);
  or or_5 (or_5_out, and_11_out, and_15_out);
  or or_6 (or_6_out, and_19_out, and_23_out);
  or or_7 (or_7_out, and_12_out, and_16_out);
  or or_8 (or_8_out, and_20_out, and_24_out);
  or or_9 (or_9_out, or_1_out, or_2_out);
  or or_10 (or_10_out, or_3_out, or_4_out);
  or or_11 (or_11_out, or_5_out, or_6_out);
  or or_12 (or_12_out, or_7_out, or_8_out);
  Switch switch_1 (.A(in_3), .B(out_7));
  Switch switch_2 (.A(in_5), .B(out_9));
  Switch switch_3 (.A(in_4), .B(out_8));
  Switch switch_4 (.A(or_11_out), .B(out_8));
  Switch switch_5 (.A(or_12_out), .B(out_7));
  Switch switch_6 (.A(in_6), .B(out_10));
  Switch switch_7 (.A(or_10_out), .B(out_9));
  Switch switch_8 (.A(or_9_out), .B(out_10));
  Switch switch_9 (.A(switch_9_a), .B(out_10));
  Switch switch_10 (.A(switch_10_a), .B(out_9));
  Switch switch_11 (.A(switch_11_a), .B(out_8));
  Switch switch_12 (.A(switch_12_a), .B(out_7));
  D_FF d_ff_17 (.D(out_7), .C(write_into_register_A), .Q(d_ff_17_q));  // open: nQ
  D_FF d_ff_18 (.D(out_8), .C(write_into_register_A), .Q(d_ff_18_q));  // open: nQ
  D_FF d_ff_19 (.D(out_9), .C(write_into_register_A), .Q(d_ff_19_q));  // open: nQ
  D_FF d_ff_20 (.D(out_10), .C(write_into_register_A), .Q(d_ff_20_q));  // open: nQ
  Add add_1 (.a(d_ff_17_q), .b(xor_1_out), .c_i(add_2_c_o), .s(switch_12_a));  // open: c_o
  Add add_2 (.a(d_ff_18_q), .b(xor_2_out), .c_i(add_3_c_o), .s(switch_11_a), .c_o(add_2_c_o));
  Add add_3 (.a(d_ff_19_q), .b(xor_3_out), .c_i(add_4_c_o), .s(switch_10_a), .c_o(add_3_c_o));
  D_FF d_ff_21 (.D(out_7), .C(write_into_register_B), .Q(d_ff_21_q));  // open: nQ
  xor xor_1 (xor_1_out, d_ff_21_q, Add_Subtract);
  D_FF d_ff_22 (.D(out_8), .C(write_into_register_B), .Q(d_ff_22_q));  // open: nQ
  D_FF d_ff_23 (.D(out_9), .C(write_into_register_B), .Q(d_ff_23_q));  // open: nQ
  xor xor_2 (xor_2_out, d_ff_22_q, Add_Subtract);
  Add add_4 (.a(d_ff_20_q), .b(xor_4_out), .c_i(Add_Subtract), .s(switch_9_a), .c_o(add_4_c_o));
  D_FF d_ff_24 (.D(out_10), .C(write_into_register_B), .Q(d_ff_24_q));  // open: nQ
  xor xor_3 (xor_3_out, d_ff_23_q, Add_Subtract);
  xor xor_4 (xor_4_out, d_ff_24_q, Add_Subtract);
endmodule
